// Logisim project Guia_2.circ as structural Verilog: 1 circuit, main circuit main
module main (
  input  in_1,
  input  in_2,
  input  in_3,
  input  in_4,
  input  in_5,
  input  in_6,
  input  in_7,
  input  in_8,
  input  in_9,
  input  in_10,
  input  in_11,
  input  in_12,
  input  in_13,
  input  in_14,
  input  in_15,
  input  in_16,
  input  in_17,
  input  in_18,
  input  \input ,
  input  in_20,
  input  in_21,
  input  in_22,
  input  in_23,
  input  in_24,
  input  in_25,
  input  in_26,
  input  in_27,
  input  in_28,
  input  in_29,
  input  in_30,
  input  in_31,
  input  in_32,
  input  in_33,
  input  in_34,
  input  in_35,
  output out_36,
  output out_37,
  output out_38,
  output out_39,
  output out_40,
  output out_41,
  output out_42,
  output out_43,
  output out_44,
  output out_45,
  output out_46,
  output _0__tiene_inv,
  output _00,
  output _01,
  output _10,
  output _11,
  output out_52,
  output out_53,
  output out_54,
  output out_55,
  output out_56,
  output out_57,
  output out_58,
  output out_59,
  output out_60,
  output out_61,
  output out_62,
  output out_63,
  output out_64
);

  wire and_1_out, and_3_out, and_4_out, and_5_out, and_6_out, and_7_out, and_10_out, and_11_out, and_12_out,
       and_13_out, and_14_out, and_15_out, and_16_out, and_17_out, and_18_out, and_19_out, and_20_out,
       and_21_out, and_26_out, and_27_out, and_28_out, and_29_out, and_30_out, d_ff_4_q, d_ff_5_q, d_ff_6_q,
       nand_1_out, nor_1_out, not_1_out, not_2_out, not_3_out, not_4_out, not_5_out, not_6_out, not_7_out,
       not_8_out, not_9_out, not_10_out, not_11_out, not_12_out, not_13_out, not_14_out, not_15_out,
       not_16_out, not_17_out, not_18_out, not_19_out, not_20_out, or_1_out, or_2_out, xor_1_out;

  not not_1 (not_1_out, in_3);
  not not_2 (not_2_out, in_4);
  or or_1 (or_1_out, in_5, in_6);
  and and_1 (and_1_out, in_6, not_3_out);
  not not_3 (not_3_out, in_8);
  not not_4 (not_4_out, in_13);
  not not_5 (not_5_out, in_14);
  not not_6 (not_6_out, in_15);
  not not_7 (not_7_out, in_16);
  not not_8 (not_8_out, in_17);
  not not_9 (not_9_out, in_18);
  and and_2 (out_37, in_2, in_1);
  nor nor_1 (nor_1_out, in_7, in_8);
  nand nand_1 (nand_1_out, in_5, in_6);
  and and_3 (and_3_out, nand_1_out, in_7);
  and and_4 (and_4_out, not_4_out, 1'b1);
  and and_5 (and_5_out, not_5_out, and_4_out);
  and and_6 (and_6_out, not_6_out, and_5_out);
  and and_7 (and_7_out, not_8_out, not_9_out);
  not not_10 (not_10_out, in_18);
  not not_11 (not_11_out, in_17);
  and and_8 (out_38, not_1_out, not_2_out);
  xor xor_1 (xor_1_out, or_1_out, nor_1_out);
  or or_2 (or_2_out, and_3_out, and_1_out);
  xor xor_2 (out_40, in_9, in_10);
  xor xor_3 (out_41, in_9, in_11);
  xor xor_4 (out_42, in_9, in_12);
  xor xor_5 (out_46, not_4_out, 1'b1);
  xor xor_6 (out_45, and_4_out, not_5_out);
  and and_9 (_00, and_7_out, \input );
  and and_10 (and_10_out, in_17, not_10_out);
  and and_11 (and_11_out, not_11_out, in_18);
  and and_12 (and_12_out, in_17, in_18);
  and and_13 (and_13_out, in_21, not_12_out);
  not not_12 (not_12_out, in_20);
  not not_13 (not_13_out, in_22);
  and and_14 (and_14_out, not_13_out, not_14_out);
  not not_14 (not_14_out, in_23);
  and and_15 (and_15_out, in_22, not_15_out);
  not not_15 (not_15_out, in_20);
  not not_16 (not_16_out, in_21);
  and and_16 (and_16_out, not_16_out, not_17_out);
  not not_17 (not_17_out, in_23);
  and and_17 (and_17_out, in_23, not_18_out);
  not not_18 (not_18_out, in_20);
  not not_19 (not_19_out, in_22);
  and and_18 (and_18_out, not_19_out, not_20_out);
  not not_20 (not_20_out, in_21);
  and and_19 (and_19_out, in_34, out_60);
  and and_20 (and_20_out, out_61, and_19_out);
  and and_21 (and_21_out, and_20_out, out_62);
  xor xor_7 (out_36, in_1, in_2);
  and and_22 (out_39, xor_1_out, or_2_out);
  xor xor_8 (out_44, and_5_out, not_6_out);
  xor xor_9 (out_43, not_7_out, and_6_out);
  and and_23 (_01, and_10_out, \input );
  and and_24 (_10, and_11_out, \input );
  and and_25 (_11, and_12_out, \input );
  and and_26 (and_26_out, and_13_out, and_14_out);
  and and_27 (and_27_out, and_15_out, and_16_out);
  and and_28 (and_28_out, and_17_out, and_18_out);
  and and_29 (and_29_out, in_27, in_29);
  and and_30 (and_30_out, in_30, in_32);
  D_Flip_Flop d_ff_1 (.D(in_24), .clk(and_29_out), .Q(out_54), .reset(in_28));  // open: Qn, preset
  D_Flip_Flop d_ff_2 (.D(in_25), .clk(and_29_out), .Q(out_55), .reset(in_28));  // open: Qn, preset
  D_Flip_Flop d_ff_3 (.D(in_26), .clk(and_29_out), .Q(out_56), .reset(in_28));  // open: Qn, preset
  D_Flip_Flop d_ff_4 (.D(out_57), .clk(and_30_out), .Q(d_ff_4_q), .reset(in_31));  // open: Qn, preset
  D_Flip_Flop d_ff_5 (.D(out_58), .clk(and_30_out), .Q(d_ff_5_q), .reset(in_31));  // open: Qn, preset
  D_Flip_Flop d_ff_6 (.D(out_59), .clk(and_30_out), .Q(d_ff_6_q), .reset(in_31));  // open: Qn, preset
  J_K_Flip_Flop j_k_ff_1 (.J(in_34), .K(in_34), .clk(in_35), .Q(out_60));  // open: Qn, preset, reset
  J_K_Flip_Flop j_k_ff_2 (.J(and_19_out), .K(and_19_out), .clk(in_35), .Q(out_61));  // open: Qn, preset, reset
  J_K_Flip_Flop j_k_ff_3 (.J(and_20_out), .K(and_20_out), .clk(in_35), .Q(out_62));  // open: Qn, preset, reset
  J_K_Flip_Flop j_k_ff_4 (.J(and_21_out), .K(and_21_out), .clk(in_35), .Q(out_63));  // open: Qn, preset, reset
  and and_31 (_0__tiene_inv, out_43, in_16);
  buf or_3 (out_52, and_28_out);  // OR_Gate
  assign out_57 = in_33 ? d_ff_4_q : 1'bz;  // Controlled_Buffer controlled_buffer_1
  assign out_58 = in_33 ? d_ff_5_q : 1'bz;  // Controlled_Buffer controlled_buffer_2
  assign out_59 = in_33 ? d_ff_6_q : 1'bz;  // Controlled_Buffer controlled_buffer_3
  or or_4 (out_53, and_28_out, and_27_out);
  and and_32 (out_64, out_63, and_21_out);

  // Notes on the sheet:
  //   5)
  //   4.b)
  //   4.c)
  //   7)
  //   Half Adder
  //   Contador de 4 bits
  //   Inverso aditivo
  //   1: no tiene inv
  //   Falta hacer identificador de 2 prendidos
endmodule
