// Logisim project HalfAdderProyect.circ as structural Verilog: 2 circuits, main circuit main
module main (
  input  in_1,
  input  in_2,
  output out_3,
  output out_4
);

  and and_1 (out_4, in_1, in_2);
  xor xor_1 (out_3, in_1, in_2);
endmodule

module HalfAdder (
  input  in_1,
  input  in_2,
  output out_3,
  output out_4
);

  main main_1 (.in_1(in_1), .in_2(in_2), .out_3(out_3), .out_4(out_4));
endmodule
